// Logisim project sandbox.circ as structural Verilog: 1 circuit, main circuit main
module main (
);

  wire and_1_out, Branch, registerfile_1_p3, registerfile_1_p4, Tick, Zero;
  wire [4:0] Register_A, Register_B;
  wire [5:0] Control_p2;
  wire [9:0] Control_p3;
  wire [15:0] mipsprogramrom_1_p1;
  wire [31:0] adder_1_p3, adder_2_p3, bit_extender_1_out, multiplexer_1_out, PC_q, shifter_1_out;

  Clock clock_1 (.out(Tick));
  Register #(.width(32)) PC (.D(multiplexer_1_out), .Q(PC_q), .clk(Tick));  // open: en, clr
  Register #(.width(6)) OpCode (.D(Control_p2), .clk(Tick));  // open: en, Q, clr
  Multiplexer #(.width(32), .enable("false")) multiplexer_1 (
    .in0(adder_2_p3), .in1(adder_1_p3), .out(multiplexer_1_out), .sel(and_1_out));
  and and_1 (and_1_out, Branch, Zero);
  // Adder adder_1: pin names not known; wires that end beside it: PC_q, 32'h4, adder_1_p3
  // PLA Control: pin names not known; wires that end beside it: PC_q, Control_p2, {Control_p3[9:3], Branch, Control_p3[1:0]}, Control_p3[9], Control_p3[8], Control_p3[7], Control_p3[6:5], Control_p3[4], Control_p3[3]
  assign bit_extender_1_out = {{16{mipsprogramrom_1_p1[15]}}, mipsprogramrom_1_p1};  // Bit_Extender bit_extender_1
  // MIPSProgramROM mipsprogramrom_1: pin names not known; wires that end beside it: {Control_p2, Register_A, Register_B, mipsprogramrom_1_p1[4:0], mipsprogramrom_1_p1[9:5], mipsprogramrom_1_p1[15:10]}
  Shifter #(.width(32)) shifter_1 (.in(bit_extender_1_out), .\dist (5'b00010), .out(shifter_1_out));
  // Adder adder_2: pin names not known; wires that end beside it: adder_1_p3, shifter_1_out, adder_2_p3
  // RegisterFile registerfile_1: pin names not known; wires that end beside it: Register_A, Register_B, registerfile_1_p3, registerfile_1_p4
  // MIPS_ALU mips_alu_1: pin names not known; wires that end beside it: registerfile_1_p3, registerfile_1_p4, Zero
endmodule
